// Logisim project traffic_light.circ as structural Verilog: 1 circuit, main circuit main
module main (
  input  TA,
  input  TaL,
  input  TB,
  input  TbL
);

  wire and_2_out, and_3_out, and_5_out, and_6_out, and_8_out, and_9_out, and_10_out, and_11_out, and_12_out,
       clock_1_out, comparator_1_eq, comparator_2_eq, comparator_3_eq, comparator_4_eq, comparator_5_eq,
       comparator_6_eq, comparator_7_eq, comparator_8_eq, not_1_out, not_2_out, not_3_out, not_4_out,
       not_5_out, not_6_out, not_7_out, not_8_out, not_9_out, not_10_out, not_11_out, not_12_out, not_13_out,
       not_14_out, not_15_out, not_16_out, not_17_out, not_18_out, not_19_out, not_22_out, not_23_out,
       not_24_out, not_25_out, not_26_out, not_27_out, or_8_out, or_9_out;
  wire [0:0] or_1_out;
  wire [1:0] not_21_out;
  wire [1:1] and_7_out, not_20_out, or_4_out;
  wire [2:0] and_1_out, d_ff_1_q, multiplexer_1_out, or_6_out;

  Clock clock_1 (.out(clock_1_out));
  not not_1 (not_1_out, TaL);
  not not_2 (not_2_out, TA);
  not not_3 (not_3_out, TB);
  not not_4 (not_4_out, TbL);
  not not_5 (not_5_out, TA);
  not not_6 (not_6_out, TaL);
  not not_7 (not_7_out, TA);
  not not_8 (not_8_out, TaL);
  not not_9 (not_9_out, TA);
  not not_10 (not_10_out, TA);
  not not_11 (not_11_out, TaL);
  not not_12 (not_12_out, TA);
  or or_1 (or_1_out[0], TA, not_1_out, TB, TbL);
  and and_1 (and_1_out[1], not_2_out, TaL, not_3_out, not_4_out);
  not not_13 (not_13_out, TA);
  not not_14 (not_14_out, TB);
  not not_15 (not_15_out, TbL);
  and and_2 (and_2_out, not_5_out, not_6_out, TB);
  and and_3 (and_3_out, not_7_out, not_8_out, TbL);
  and and_4 (or_6_out[1], not_9_out, TaL);
  and and_5 (and_5_out, not_10_out, not_11_out);
  and and_6 (and_6_out, not_12_out, TaL);
  or or_2 (and_1_out[2], TB, TbL);
  and and_7 (and_7_out[1], not_13_out, TaL, not_14_out, not_15_out);
  or or_3 (or_6_out[2], and_2_out, and_3_out);
  or or_4 (or_4_out[1], and_5_out, and_6_out);
  D_Flip_Flop d_ff_1 (.D(multiplexer_1_out[0]), .clk(clock_1_out), .Q(d_ff_1_q[0]));  // open: Qn, preset, reset
  D_Flip_Flop d_ff_2 (.D(multiplexer_1_out[1]), .clk(clock_1_out), .Q(d_ff_1_q[1]));  // open: Qn, preset, reset
  D_Flip_Flop d_ff_3 (.D(multiplexer_1_out[2]), .clk(clock_1_out), .Q(d_ff_1_q[2]));  // open: Qn, preset, reset
  not not_16 (not_16_out, TaL);
  not not_17 (not_17_out, TbL);
  not not_18 (not_18_out, TB);
  and and_8 (and_8_out, not_16_out, not_18_out, TbL);
  or or_5 (not_21_out[1], TB, not_17_out);
  not not_19 (not_19_out, TB);
  or or_6 (or_6_out[0], TA, and_8_out);
  and and_9 (and_9_out, TA, not_19_out);
  and and_10 (and_10_out, not_19_out, TbL);
  not not_20 (not_20_out[1], TB);
  or or_7 (and_1_out[0], and_9_out, and_10_out);
  not not_21 (not_21_out[0], not_21_out[1]);
  Multiplexer #(.select(3), .width(3)) multiplexer_1 (
    .in0(or_6_out), .in1({1'b0, or_4_out[1], 1'b1}), .in2({2'b01, or_1_out[0]}), .in3(and_1_out),
    .in4({1'b1, not_20_out[1], 1'b0}), .in5({1'b1, not_21_out}),
    .in6({and_1_out[2], and_7_out[1], and_1_out[0]}), .out(multiplexer_1_out), .sel(d_ff_1_q));  // open: in7
  Comparator #(.width(3)) comparator_1 (.a(d_ff_1_q), .b(3'b000), .eq(comparator_1_eq));  // open: gt, lt
  Comparator #(.width(3)) comparator_2 (.a(d_ff_1_q), .b(3'b011), .eq(comparator_2_eq));  // open: gt, lt
  Comparator #(.width(3)) comparator_3 (.a(d_ff_1_q), .b(3'b001), .eq(comparator_3_eq));  // open: gt, lt
  Comparator #(.width(3)) comparator_4 (.a(d_ff_1_q), .b(3'b010), .eq(comparator_4_eq));  // open: gt, lt
  Comparator #(.width(3)) comparator_5 (.a(d_ff_1_q), .b(3'b000), .eq(comparator_5_eq));  // open: gt, lt
  Comparator #(.width(3)) comparator_6 (.a(d_ff_1_q), .b(3'b110), .eq(comparator_6_eq));  // open: gt, lt
  Comparator #(.width(3)) comparator_7 (.a(d_ff_1_q), .b(3'b100), .eq(comparator_7_eq));  // open: gt, lt
  Comparator #(.width(3)) comparator_8 (.a(d_ff_1_q), .b(3'b101), .eq(comparator_8_eq));  // open: gt, lt
  not not_22 (not_22_out, comparator_2_eq);
  not not_23 (not_23_out, comparator_3_eq);
  not not_24 (not_24_out, comparator_8_eq);
  not not_25 (not_25_out, comparator_7_eq);
  not not_26 (not_26_out, comparator_6_eq);
  and and_11 (and_11_out, not_22_out, not_23_out, not_27_out);
  not not_27 (not_27_out, comparator_4_eq);
  or or_8 (or_8_out, and_11_out, comparator_1_eq);
  or or_9 (or_9_out, comparator_5_eq, and_12_out);
  and and_12 (and_12_out, not_24_out, not_25_out, not_26_out);
  LED A (.in(or_8_out));
  LED led_1 (.in(comparator_2_eq));
  LED led_2 (.in(comparator_3_eq));
  LED led_3 (.in(comparator_4_eq));
  LED B (.in(or_9_out));
  LED led_4 (.in(comparator_6_eq));
  LED led_5 (.in(comparator_7_eq));
  LED led_6 (.in(comparator_8_eq));
endmodule
